# Fritzing sketch LedTestScheme (saved by Fritzing 0.9.3b)
breadboards: 1

parts:
  MOTOR1 = 28BYJ-48 Stepper Motor
  Part2 = KY-003 Hall Magnetic Sensor Module [package="Breakout board"]
  Part3 = EasyDriver_v44
  Part4 = EasyDriver_v44
  R3 = Resistor [tolerance=±5% resistance=10k package=THT]
  R4 = Resistor [tolerance=±5% resistance=10k package=THT]
  LED1 = LED - 5mm [color="Red (633nm)" package="5 mm [THT]"]
  M1 = Stepper Motor - Bipolar
  Power_plug1 = Power plug
  R5 = Resistor [tolerance=±5% resistance=1k package=THT]
  Part5 = KY-003 Hall Magnetic Sensor Module [package="Breakout board"]
  R6 = PHOTOCELL [package=photocell-kit]
  R7 = PHOTOCELL [package=photocell-kit]
  Part6 = Arduino Uno (Rev3)

nets:
  N1: MOTOR1.ORANGE, Part4.OUT1B
  N2: MOTOR1.YELLOW, Part4.OUT1A
  N3: MOTOR1.PINK, Part4.OUT2B
  N4: MOTOR1.BLUE, Part4.OUT2A
  N5: Part2.S, Part6.D7
  VIN: Part2.Vin, Part6.3V3
  GND: Part2.-, Part3.GND, Part4.GND, R3.Pin_1, R4.Pin_1, LED1.cathode, Power_plug1.GND, Part6.GND
  N6: Part3.V+, Part4.V+, Power_plug1.VCC
  N7: Part3.STEP, Part6.D8
  N8: Part3.DIR, Part6.D9_PWM
  N9: Part3.OUT2A, M1.A
  N10: Part3.OUT2B, M1.C
  N11: Part3.OUT1A, M1.B
  N12: Part3.OUT1B, M1.D
  N13: Part3.MS1, Part6.D10_PWM/SS
  N14: Part3.MS2, Part6.D11_PWM/MOSI
  N15: Part4.STEP, Part6.D2
  N16: Part4.DIR, Part6.D3_PWM
  N17: Part4.MS1, Part6.D4
  N18: Part4.SLEEP, Part6.D12/MISO
  N19: Part4.MS2, Part6.D5_PWM
  N20: R3.Pin_0, R7.P$2
  N21: R4.Pin_0, R6.P$2
  N22: LED1.anode, R5.Pin_1
  N23: R5.Pin_0, Part6.D13/SCK
  N24: Part5.S, Part6.D6_PWM
  N25: R6.P$1, Part6.5V

notes:
  12V
  HallA
  HallB
  LightSensorA
  LightSensorB
  Wire Color Legend
  ================
  General:
  > red +VCC
  > black -GND
  > yellow - Digital Read
  > green - Analog Read
  Motor Driver:
  > cyan - DIR
  > orange - STEP
  > gray - MS1
  > pink - MS2
  > blue - SLP
  Doesn't apply to motor -driver connections, depends on given motor's wires.

custom parts:
  KY-003 Hall Magnetic Sensor Module: KEYES KY-003 Arduino Hall Magnetic Sensor Module is a switch that will turn on/off in the presence of a magnetic field.
